// Digital circuit part_c.dig as structural Verilog
module part_c (
  input  in_0,
  input  in_1,
  input  in_2,
  output out_0
);

  wire nfet_4_s, nfet_6_s, nfet_8_s, nfet_13_d, pfet_1_d, pfet_2_d, pfet_3_d, pfet_4_d, pfet_5_d, pfet_6_d,
       pfet_10_d, pfet_11_d, pfet_12_d, pfet_13_d, pfet_14_d;

  PFET pfet_1 (.G(in_0), .S(1'b1), .D(pfet_1_d));
  NFET nfet_1 (.G(in_0), .D(pfet_1_d), .S(1'b0));
  PFET pfet_2 (.G(in_1), .S(1'b1), .D(pfet_2_d));
  NFET nfet_2 (.G(in_1), .D(pfet_2_d), .S(1'b0));
  PFET pfet_3 (.G(in_2), .S(1'b1), .D(pfet_3_d));
  NFET nfet_3 (.G(in_2), .D(pfet_3_d), .S(1'b0));
  PFET pfet_4 (.G(pfet_1_d), .S(1'b1), .D(pfet_4_d));
  NFET nfet_4 (.G(pfet_1_d), .D(pfet_4_d), .S(nfet_4_s));
  NFET nfet_5 (.G(pfet_3_d), .D(nfet_4_s), .S(1'b0));
  PFET pfet_5 (.G(in_0), .S(1'b1), .D(pfet_5_d));
  PFET pfet_6 (.G(in_0), .S(1'b1), .D(pfet_6_d));
  PFET pfet_7 (.G(pfet_3_d), .S(1'b1), .D(pfet_4_d));
  PFET pfet_8 (.G(in_2), .S(1'b1), .D(pfet_5_d));
  NFET nfet_6 (.G(in_0), .D(pfet_5_d), .S(nfet_6_s));
  NFET nfet_7 (.G(in_2), .D(nfet_6_s), .S(1'b0));
  PFET pfet_9 (.G(pfet_2_d), .S(1'b1), .D(pfet_6_d));
  NFET nfet_8 (.G(in_0), .D(pfet_6_d), .S(nfet_8_s));
  NFET nfet_9 (.G(pfet_2_d), .D(nfet_8_s), .S(1'b0));
  PFET pfet_10 (.G(pfet_4_d), .S(1'b1), .D(pfet_10_d));
  NFET nfet_10 (.G(pfet_4_d), .D(pfet_10_d), .S(1'b0));
  PFET pfet_11 (.G(pfet_5_d), .S(1'b1), .D(pfet_11_d));
  NFET nfet_11 (.G(pfet_5_d), .D(pfet_11_d), .S(1'b0));
  PFET pfet_12 (.G(pfet_6_d), .S(1'b1), .D(pfet_12_d));
  NFET nfet_12 (.G(pfet_6_d), .D(pfet_12_d), .S(1'b0));
  NFET nfet_13 (.G(pfet_10_d), .D(nfet_13_d), .S(1'b0));
  PFET pfet_13 (.G(pfet_10_d), .S(1'b1), .D(pfet_13_d));
  PFET pfet_14 (.G(pfet_11_d), .S(pfet_13_d), .D(pfet_14_d));
  PFET pfet_15 (.G(pfet_12_d), .S(pfet_14_d), .D(nfet_13_d));
  NFET nfet_14 (.G(pfet_12_d), .D(nfet_13_d), .S(1'b0));
  NFET nfet_15 (.G(pfet_11_d), .D(nfet_13_d), .S(1'b0));
  PFET pfet_16 (.G(nfet_13_d), .S(1'b1), .D(out_0));
  NFET nfet_16 (.G(nfet_13_d), .D(out_0), .S(1'b0));
endmodule

/* Test case part_c_test:
in_0 in_1 in_2 out_0
  0    0    0     1
  0    0    1     0
  0    1    0     1
  0    1    1     0
  1    0    0     1
  1    0    1     1
  1    1    0     0
  1    1    1     1
*/
